# Fritzing sketch IngegnoRetroGamingWiring (saved by Fritzing 0.9.3b)
breadboards: 1

parts:
  Onderdeel1 = Arduino Nano (Rev3.0)
  Onderdeel2 = Thumb Joystick
  VCC1 = Battery block 9V
  U1 = SWITCH_SPDT [package=kps-1290]
  S4 = Pushbutton [package="[SMD]"]
  S5 = Pushbutton [package="[SMD]"]
  Onderdeel3 = TFT 1.8 inch 160x128 w microSD [part_number=358]

nets:
  GND: Onderdeel1.GND, Onderdeel2.GND, U1.S, S4.Pin_1, S4.Pin_2, S5.Pin_1, S5.Pin_2, Onderdeel3.GND
  N1: Onderdeel1.D2, S4.Pin_3, S4.Pin_4
  N2: Onderdeel1.D3, S5.Pin_3, S5.Pin_4
  N3: Onderdeel1.D4, Onderdeel2.SEL
  N4: Onderdeel1.D8, Onderdeel3.RESET
  N5: Onderdeel1.D9, Onderdeel3.AO
  N6: Onderdeel1.D10, Onderdeel3.CS
  N7: Onderdeel1.D11/MOSI, Onderdeel3.SDA
  N8: Onderdeel1.VIN, VCC1.+
  VCC: Onderdeel1.5V, Onderdeel2.VCC, Onderdeel3.VCC
  N9: Onderdeel1.A2, Onderdeel2.VERT
  N10: Onderdeel1.A1, Onderdeel2.HORZ
  N11: Onderdeel1.3V3, Onderdeel3.LED
  N12: Onderdeel1.D13/SCK, Onderdeel3.SCK
  N13: VCC1.-, U1.P

notes:
  LEFT A Button
  RIGHT B Btn
  Joystick Button

custom parts:
  TFT 1.8 inch 160x128 w microSD: This lovely little display breakout is the best way to add a small, colorful and bright display to any project. Since the display uses 4-wire SPI to communicate and has its own pixel-addressable frame buffer, it can be used with every kind of microcontroller. Even a very small one with low memory and few pins available! The 1.8" display has 128x160 color pixels.
